# Fritzing sketch ESP32-LED_Strip (saved by Fritzing 0.9.4)
breadboards: 1

parts:
  ESP32-S2 = Adafruit QT Py ESP32-S2 [part_number="Adafruit #5325"]
  Q2_Green = MOSFET-NCHANNEL [part_number=IRF3708 package=to220v]
  Q3_Blue = MOSFET-NCHANNEL [part_number=IRF3708 package=to220v]
  Q1_Red = MOSFET-NCHANNEL [part_number=IRF3708 package=to220v]
  R1 = Resistor [tolerance=±5% resistance=1k package=THT]
  R2 = Resistor [tolerance=±5% resistance=1k package=THT]
  R3 = Resistor [tolerance=±5% resistance=1k package=THT]
  R4 = Resistor [tolerance=±5% resistance=1k package=THT]
  Q4_White = MOSFET-NCHANNEL [part_number=IRF3708 package=to220v]
  LED1_RGBW_12V_strip = RGB LED (com. cathode, rgb) [part_number="+12, G, R, W, B" package="5 mm [THT]"]
  AC-DC_12V = HLK-PM12 [part_number="10A 120W"]

nets:
  N1: ESP32-S2.GND, Q2_Green.S, Q3_Blue.S, Q1_Red.S, Q4_White.S, LED1_RGBW_12V_strip.green_anode, AC-DC_12V.-Vo
  N2: ESP32-S2.A0, R1.Pin_1
  N3: ESP32-S2.A1, R2.Pin_1
  N4: ESP32-S2.A2, R3.Pin_1
  N5: ESP32-S2.A3, R4.Pin_1
  N6: Q2_Green.G, R2.Pin_0
  N7: Q2_Green.D, LED1_RGBW_12V_strip.red_anode
  N8: Q3_Blue.G, R3.Pin_0
  N9: Q3_Blue.D, LED1_RGBW_12V_strip.blue_anode
  N10: Q1_Red.G, R1.Pin_0
  N11: Q1_Red.D, LED1_RGBW_12V_strip.common_cathode
  N12: R4.Pin_0, Q4_White.G

custom parts:
  Adafruit QT Py ESP32-S2: What has your favorite Espressif WiFi microcontroller, comes with our favorite connector - the STEMMA QT, a chainable I2C port, and has lots of Flash and RAM memory for your next IoT project? What will make your next IoT project flyyyyy? What a cutie pie! Or is it... a QT Py? This diminutive dev board comes with one of our new favorite lil chips, the ESP32-S2! The ESP32-S2 is a highly-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
